// Logisim project 16-bit ALU.circ as structural Verilog: 7 circuits, main circuit main
// ALU
module _16_bit_b (
  input  [15:0] A,
  input  [15:0] B,
  input  ALUop,
  input  [2:0] Operation,
  input  Cin,
  input  Cin_2,
  output [15:0] Result,
  output Result_2,
  output Cout,
  output Cout_2
);

  wire comparator_1_gt, comparator_1_lt;
  wire [15:0] adder_1_out, AND_out, bit_extender_1_out, NOR_out, OR_out, subtractor_1_out, undriven, XOR_out;

  assign AND_out = A & B;  // AND_Gate AND, 16 bits wide
  assign OR_out = A | B;  // OR_Gate OR, 16 bits wide
  assign XOR_out = A ^ B;  // XOR_Gate XOR, 16 bits wide
  assign NOR_out = ~(A | B);  // NOR_Gate NOR, 16 bits wide
  Adder #(.width(16)) adder_1 (.a(A), .b(B), .out(adder_1_out), .cin(Cin), .cout(Cout));
  Subtractor #(.width(16)) subtractor_1 (.a(A), .b(B), .out(subtractor_1_out), .bin(Cin_2), .bout(Cout_2));
  Subtractor #(.width(16)) subtractor_2 (.a(A), .b(B), .out(subtractor_1_out), .bin(Cin_2), .bout(Cout_2));
  Comparator #(.width(16)) comparator_1 (
    .a(A), .b(B), .gt(comparator_1_gt), .eq(comparator_1_gt), .lt(comparator_1_lt));
  assign bit_extender_1_out = {{15{1'b0}}, comparator_1_lt};  // Bit_Extender bit_extender_1
  assign bit_extender_1_out = {{15{1'b0}}, comparator_1_lt};  // Bit_Extender bit_extender_2
  Multiplexer #(.select(3), .width(16)) multiplexer_1 (
    .in0(AND_out), .in1(OR_out), .in2(XOR_out), .in3(NOR_out), .in4(adder_1_out), .in5(subtractor_1_out),
    .in6(bit_extender_1_out), .in7(undriven), .out(Result), .sel(Operation), .en(ALUop));
  Multiplexer #(.select(3), .width(16)) multiplexer_2 (
    .in0(AND_out), .in1(OR_out), .in2(XOR_out), .in3(NOR_out), .in4(adder_1_out), .in5(subtractor_1_out),
    .in6(bit_extender_1_out), .in7(undriven), .out(Result), .sel(Operation), .en(ALUop));
  nor nor_2 (Result_2, Result[0], Result[1], Result[2], Result[3], Result[4], Result[5], Result[6], Result[7], Result[8], Result[9], Result[10], Result[11], Result[12], Result[13], Result[14], Result[15]);
endmodule

module main (
  input  Cout
);

  wire ALUop, ALUSrc, and_1_out, branch, button_1_out, clock_1_out, Enable, jump, main_1_regwrite, MemRead,
       MemReg, MemWrite, n16_bit_b_1_result_2, RegDst;
  wire [2:0] main_2_o0;
  wire [3:0] multiplexer_1_out, opcode;
  wire [11:0] adder_1_out, adder_2_out, bit_extender_2_out, multiplexer_4_out, ram_1_data, register_1_q, toPC;
  wire [15:0] bit_extender_1_out, multiplexer_2_out, multiplexer_3_out, n16_bit_b_1_result, ram_2_data,
       register_file_1_read_data_1, register_file_1_read_data_2;

  FcontrolUnit_main main_1 (
    .in_1(opcode), .ALUsrc(ALUSrc), .ALUop(ALUop), .memRead(MemRead), .memWrite(MemWrite),
    .RegWrite(main_1_regwrite), .memToReg(MemReg), .RegDst(RegDst), .Branch(branch), .Jump(jump));
  Register #(.width(12)) register_1 (.D(toPC), .Q(register_1_q), .clk(clock_1_out), .clr(button_1_out));  // open: en
  Button button_1 (.out(button_1_out));
  Clock clock_1 (.out(clock_1_out));
  Adder #(.width(12)) adder_1 (.a(register_1_q), .b(12'h1), .out(adder_1_out));  // open: cin, cout
  alu_control_main main_2 (
    .ALUop(ALUop), .O2(main_2_o0[2]), .I3(opcode[3]), .I2(opcode[2]), .O1(main_2_o0[1]), .I1(opcode[1]),
    .O0(main_2_o0[0]), .I0(opcode[0]), .Enable(Enable));
  RAM #(.addrWidth(12), .dataWidth(16)) ram_1 (
    .addr(register_1_q), .data({opcode, ram_1_data}));  // open: sel, clk, ld, clr
  Multiplexer #(.width(4), .enable("false")) multiplexer_1 (
    .in0(ram_1_data[7:4]), .in1(ram_1_data[3:0]), .out(multiplexer_1_out), .sel(RegDst));
  register_file register_file_1 (
    .Clock(clock_1_out), .read_data_1(register_file_1_read_data_1),
    .read_data_2(register_file_1_read_data_2), .RA(ram_1_data[11:8]), .write_register(multiplexer_1_out),
    .RB(ram_1_data[7:4]), .regWrite(main_1_regwrite), .data(multiplexer_3_out));
  assign bit_extender_1_out = {{12{1'b0}}, ram_1_data[3:0]};  // Bit_Extender bit_extender_1
  // Probe on multiplexer_2_out
  // Probe on register_file_1_read_data_1
  Multiplexer #(.width(16), .enable("false")) multiplexer_2 (
    .in0(register_file_1_read_data_2), .in1(bit_extender_1_out), .out(multiplexer_2_out), .sel(ALUSrc));
  Bit_Extender #(.in_width(16), .out_width(12), .\type ("sign")) bit_extender_2 (
    .in(bit_extender_1_out), .out(bit_extender_2_out));
  Multiplexer #(.width(16), .enable("false")) multiplexer_3 (
    .in0(ram_2_data), .in1(n16_bit_b_1_result), .out(multiplexer_3_out), .sel(MemReg));
  _16_bit_b u_16_bit_b_1 (
    .B(multiplexer_2_out), .Result(n16_bit_b_1_result), .Result_2(n16_bit_b_1_result_2), .Cout_2(Cout),
    .Operation(main_2_o0), .A(register_file_1_read_data_1), .ALUop(Enable));  // open: Cin_2, Cout, Cin
  Adder #(.width(12)) adder_2 (.a(adder_1_out), .b(bit_extender_2_out), .out(adder_2_out));  // open: cin, cout
  and and_1 (and_1_out, branch, n16_bit_b_1_result_2);
  Multiplexer #(.width(12), .enable("false")) multiplexer_4 (
    .in0(adder_1_out), .in1(adder_2_out), .out(multiplexer_4_out), .sel(and_1_out));
  RAM #(.addrWidth(16), .dataWidth(16), .bus("separate")) ram_2 (
    .addr(n16_bit_b_1_result), .din(register_file_1_read_data_2), .data(ram_2_data), .str(MemWrite),
    .clk(clock_1_out), .ld(MemRead));  // open: sel, clr
  Multiplexer #(.width(12), .enable("false")) multiplexer_5 (
    .in0(multiplexer_4_out), .in1(ram_1_data), .out(toPC), .sel(jump));
endmodule

// 1- bit
module _1_bit_ALU (
  input  A,
  input  B,
  input  [2:0] Operation,
  input  Cin,
  input  Sub,
  input  Less,
  output Result,
  output Cout,
  output Set
);

  wire AND_out, NOR_out, OR_out, xor_1_out, XOR_2_out;

  xor xor_1 (xor_1_out, B, Sub);
  and AND (AND_out, A, B);
  or OR (OR_out, A, B);
  xor XOR_2 (XOR_2_out, A, B);
  nor NOR (NOR_out, A, B);
  Adder #(.width(1)) adder_1 (.a(A), .b(xor_1_out), .out(Set), .cin(Cin), .cout(Cout));
  Multiplexer #(.select(3)) multiplexer_1 (
    .in0(AND_out), .in1(OR_out), .in2(XOR_2_out), .in3(NOR_out), .in4(Set), .in5(Less), .out(Result),
    .sel(Operation));  // open: in6, in7, en
endmodule

// Register
module register_file (
  input  [3:0] write_register,
  input  [3:0] RA,
  input  [3:0] RB,
  input  [15:0] data,
  input  regWrite,
  input  Clock,
  output [15:0] read_data_1,
  output [15:0] read_data_2
);

  wire and_1_out, and_2_out, and_3_out, and_4_out, and_5_out, and_6_out, and_7_out, and_8_out, and_9_out,
       and_10_out, and_11_out, and_12_out, and_13_out, and_14_out, and_15_out, and_16_out, decoder_1_out0,
       decoder_1_out1, decoder_1_out2, decoder_1_out3, decoder_1_out4, decoder_1_out5, decoder_1_out6,
       decoder_1_out7, decoder_1_out8, decoder_1_out9, decoder_1_out10, decoder_1_out11, decoder_1_out12,
       decoder_1_out13, decoder_1_out14, decoder_1_out15;
  wire [15:0] a0_q, fp_q, gp_q, ra_q, s0_q, s1_q, s2_q, s3_q, s4_q, s5_q, sp_q, t0_q, t1_q, t2_q, t3_q,
       zero_q;

  Decoder #(.select(4)) decoder_1 (
    .out0(decoder_1_out0), .out1(decoder_1_out1), .out2(decoder_1_out2), .out3(decoder_1_out3),
    .out4(decoder_1_out4), .out5(decoder_1_out5), .out6(decoder_1_out6), .out7(decoder_1_out7),
    .out8(decoder_1_out8), .out9(decoder_1_out9), .out10(decoder_1_out10), .out11(decoder_1_out11),
    .out12(decoder_1_out12), .out13(decoder_1_out13), .out14(decoder_1_out14), .out15(decoder_1_out15),
    .sel(write_register));  // open: en
  and and_1 (and_1_out, decoder_1_out0, regWrite);
  and and_2 (and_2_out, decoder_1_out1, regWrite);
  and and_3 (and_3_out, decoder_1_out2, regWrite);
  and and_4 (and_4_out, decoder_1_out3, regWrite);
  and and_5 (and_5_out, decoder_1_out4, regWrite);
  and and_6 (and_6_out, decoder_1_out5, regWrite);
  and and_7 (and_7_out, decoder_1_out6, regWrite);
  and and_8 (and_8_out, decoder_1_out7, regWrite);
  Register #(.width(16)) zero (.D(data), .en(and_1_out), .Q(zero_q), .clk(Clock));  // open: clr
  Register #(.width(16)) t0 (.D(data), .en(and_2_out), .Q(t0_q), .clk(Clock));  // open: clr
  Register #(.width(16)) t1 (.D(data), .en(and_3_out), .Q(t1_q), .clk(Clock));  // open: clr
  Register #(.width(16)) t2 (.D(data), .en(and_4_out), .Q(t2_q), .clk(Clock));  // open: clr
  Register #(.width(16)) t3 (.D(data), .en(and_5_out), .Q(t3_q), .clk(Clock));  // open: clr
  Register #(.width(16)) s0 (.D(data), .en(and_6_out), .Q(s0_q), .clk(Clock));  // open: clr
  Register #(.width(16)) s1 (.D(data), .en(and_7_out), .Q(s1_q), .clk(Clock));  // open: clr
  Register #(.width(16)) s2 (.D(data), .en(and_8_out), .Q(s2_q), .clk(Clock));  // open: clr
  and and_9 (and_9_out, decoder_1_out8, regWrite);
  and and_10 (and_10_out, decoder_1_out9, regWrite);
  and and_11 (and_11_out, decoder_1_out10, regWrite);
  and and_12 (and_12_out, decoder_1_out11, regWrite);
  and and_13 (and_13_out, decoder_1_out12, regWrite);
  and and_14 (and_14_out, decoder_1_out13, regWrite);
  and and_15 (and_15_out, decoder_1_out14, regWrite);
  and and_16 (and_16_out, decoder_1_out15, regWrite);
  Register #(.width(16)) s3 (.D(data), .en(and_9_out), .Q(s3_q), .clk(Clock));  // open: clr
  Register #(.width(16)) s4 (.D(data), .en(and_10_out), .Q(s4_q), .clk(Clock));  // open: clr
  Register #(.width(16)) s5 (.D(data), .en(and_11_out), .Q(s5_q), .clk(Clock));  // open: clr
  Register #(.width(16)) gp (.D(data), .en(and_12_out), .Q(gp_q), .clk(Clock));  // open: clr
  Register #(.width(16)) sp (.D(data), .en(and_13_out), .Q(sp_q), .clk(Clock));  // open: clr
  Register #(.width(16)) fp (.D(data), .en(and_14_out), .Q(fp_q), .clk(Clock));  // open: clr
  Register #(.width(16)) u_ra (.D(data), .en(and_15_out), .Q(ra_q), .clk(Clock));  // open: clr
  Register #(.width(16)) a0 (.D(data), .en(and_16_out), .Q(a0_q), .clk(Clock));  // open: clr
  Multiplexer #(.select(4), .width(16)) multiplexer_1 (
    .in0(zero_q), .in1(t0_q), .in2(t1_q), .in3(t2_q), .in4(t3_q), .in5(s0_q), .in6(s1_q), .in7(s2_q),
    .in8(s3_q), .in9(s4_q), .in10(s5_q), .in11(gp_q), .in12(sp_q), .in13(fp_q), .in14(ra_q), .in15(a0_q),
    .out(read_data_1), .sel(RA));  // open: en
  Multiplexer #(.select(4), .width(16)) multiplexer_2 (
    .in0(zero_q), .in1(t0_q), .in2(t1_q), .in3(t2_q), .in4(t3_q), .in5(s0_q), .in6(s1_q), .in7(s2_q),
    .in8(s3_q), .in9(s4_q), .in10(s5_q), .in11(gp_q), .in12(sp_q), .in13(fp_q), .in14(ra_q), .in15(a0_q),
    .out(read_data_2), .sel(RB));  // open: en
endmodule

module Extend_block (
  input  [7:0] Input_A,
  input  Less,
  output [15:0] Imm16
);

  wire [15:0] bit_extender_1_out, bit_extender_2_out;

  assign bit_extender_1_out = {{8{1'b0}}, Input_A};  // Bit_Extender bit_extender_1
  assign bit_extender_2_out = {{8{Input_A[7]}}, Input_A};  // Bit_Extender bit_extender_2
  Multiplexer #(.width(16), .enable("false")) multiplexer_1 (
    .in0(bit_extender_1_out), .in1(bit_extender_2_out), .out(Imm16), .sel(Less));
endmodule

module Instruction_Block (
  input  [15:0] Instruction,
  output [2:0] Opcode,
  output [2:0] Rs,
  output [2:0] Rt,
  output [2:0] Rd,
  output [1:0] Shift_Amount,
  output [1:0] Function,
  output [6:0] Immediate
);


  assign Function = Instruction[1:0];
  assign Immediate = Instruction[6:0];
  assign Opcode = Instruction[15:13];
  assign Rd = Instruction[6:4];
  assign Rs = Instruction[12:10];
  assign Rt = Instruction[9:7];
  assign Shift_Amount = Instruction[3:2];
endmodule

module Control_Unit (
  input  [3:0] write_register,
  input  [3:0] RA,
  input  [3:0] RB,
  input  [15:0] in_4,
  input  regWrite,
  input  Clock,
  output [15:0] read_data_1,
  output [15:0] read_data_2
);

  wire and_1_out, and_2_out, and_3_out, and_4_out, and_5_out, and_6_out, and_7_out, and_8_out, and_9_out,
       and_10_out, and_11_out, and_12_out, and_13_out, and_14_out, and_15_out, and_16_out, decoder_1_out0,
       decoder_1_out1, decoder_1_out2, decoder_1_out3, decoder_1_out4, decoder_1_out5, decoder_1_out6,
       decoder_1_out7, decoder_1_out8, decoder_1_out9, decoder_1_out10, decoder_1_out11, decoder_1_out12,
       decoder_1_out13, decoder_1_out14, decoder_1_out15;
  wire [15:0] a0_q, fp_q, gp_q, ra_q, s0_q, s1_q, s2_q, s3_q, s4_q, s5_q, sp_q, t0_q, t1_q, t2_q, t3_q,
       zero_q;

  Decoder #(.select(4)) decoder_1 (
    .out0(decoder_1_out0), .out1(decoder_1_out1), .out2(decoder_1_out2), .out3(decoder_1_out3),
    .out4(decoder_1_out4), .out5(decoder_1_out5), .out6(decoder_1_out6), .out7(decoder_1_out7),
    .out8(decoder_1_out8), .out9(decoder_1_out9), .out10(decoder_1_out10), .out11(decoder_1_out11),
    .out12(decoder_1_out12), .out13(decoder_1_out13), .out14(decoder_1_out14), .out15(decoder_1_out15),
    .sel(write_register));  // open: en
  and and_1 (and_1_out, decoder_1_out0, regWrite);
  and and_2 (and_2_out, decoder_1_out1, regWrite);
  and and_3 (and_3_out, decoder_1_out2, regWrite);
  and and_4 (and_4_out, decoder_1_out3, regWrite);
  and and_5 (and_5_out, decoder_1_out4, regWrite);
  and and_6 (and_6_out, decoder_1_out5, regWrite);
  and and_7 (and_7_out, decoder_1_out6, regWrite);
  and and_8 (and_8_out, decoder_1_out7, regWrite);
  Register #(.width(16)) zero (.D(in_4), .en(and_1_out), .Q(zero_q), .clk(Clock));  // open: clr
  Register #(.width(16)) t0 (.D(in_4), .en(and_2_out), .Q(t0_q), .clk(Clock));  // open: clr
  Register #(.width(16)) t1 (.D(in_4), .en(and_3_out), .Q(t1_q), .clk(Clock), .clr(and_3_out));
  Register #(.width(16)) t2 (.D(in_4), .en(and_4_out), .Q(t2_q), .clk(Clock), .clr(and_4_out));
  Register #(.width(16)) t3 (.D(in_4), .Q(t3_q), .clk(Clock), .clr(and_5_out));  // open: en
  Register #(.width(16)) s0 (.D(in_4), .Q(s0_q), .clk(Clock), .clr(and_6_out));  // open: en
  Register #(.width(16)) s1 (.D(in_4), .Q(s1_q), .clk(Clock), .clr(and_7_out));  // open: en
  Register #(.width(16)) s2 (.D(in_4), .Q(s2_q), .clk(Clock), .clr(and_8_out));  // open: en
  and and_9 (and_9_out, decoder_1_out8, regWrite);
  and and_10 (and_10_out, decoder_1_out9, regWrite);
  and and_11 (and_11_out, decoder_1_out10, regWrite);
  and and_12 (and_12_out, decoder_1_out11, regWrite);
  and and_13 (and_13_out, decoder_1_out12, regWrite);
  and and_14 (and_14_out, decoder_1_out13, regWrite);
  and and_15 (and_15_out, decoder_1_out14, regWrite);
  and and_16 (and_16_out, decoder_1_out15, regWrite);
  Register #(.width(16)) s3 (.D(in_4), .Q(s3_q), .clk(Clock), .clr(and_9_out));  // open: en
  Register #(.width(16)) s4 (.D(in_4), .Q(s4_q), .clk(Clock), .clr(and_10_out));  // open: en
  Register #(.width(16)) s5 (.D(in_4), .Q(s5_q), .clk(Clock), .clr(and_11_out));  // open: en
  Register #(.width(16)) gp (.D(in_4), .Q(gp_q), .clk(Clock), .clr(and_12_out));  // open: en
  Register #(.width(16)) sp (.D(in_4), .Q(sp_q), .clk(Clock), .clr(and_13_out));  // open: en
  Register #(.width(16)) fp (.D(in_4), .Q(fp_q), .clk(Clock), .clr(and_14_out));  // open: en
  Register #(.width(16)) u_ra (.D(in_4), .Q(ra_q), .clk(Clock), .clr(and_15_out));  // open: en
  Register #(.width(16)) a0 (.D(in_4), .Q(a0_q), .clk(Clock), .clr(and_16_out));  // open: en
  Multiplexer #(.select(4), .width(16)) multiplexer_1 (
    .in0(zero_q), .in1(t0_q), .in2(t1_q), .in3(t2_q), .in4(t3_q), .in5(s0_q), .in6(s1_q), .in7(s2_q),
    .in8(s3_q), .in9(s4_q), .in10(s5_q), .in11(gp_q), .in12(sp_q), .in13(fp_q), .in14(ra_q), .in15(a0_q),
    .out(read_data_1), .sel(RA));  // open: en
  Multiplexer #(.select(4), .width(16)) multiplexer_2 (
    .in0(zero_q), .in1(t0_q), .in2(t1_q), .in3(t2_q), .in4(t3_q), .in5(s0_q), .in6(s1_q), .in7(s2_q),
    .in8(s3_q), .in9(s4_q), .in10(s5_q), .in11(gp_q), .in12(sp_q), .in13(fp_q), .in14(ra_q), .in15(a0_q),
    .out(read_data_2), .sel(RB));  // open: en
endmodule
